// Logisim project working on it.circ as structural Verilog: 1 circuit, main circuit main
module main (
);

  wire _0R_2_out, _0R_3_out, AND_1_out, AND_2_out, AND_3_out, AND_4_out, AND_5_out, AND_6_out, AND_7_out,
       AND_8_out, AND_9_out, AND_10_out, C10_out, C20_out, clock_1_out, NOT_1_out, NOT_2_out, OR_1_out,
       OR_4_out, OR_5_out, OR_6_out, Q_0_q, Q_0_qn, Q_1_q, Q_1_qn, undriven;

  Button C10 (.out(C10_out));
  Button C20 (.out(C20_out));
  not NOT_1 (NOT_1_out, C10_out);
  not NOT_2 (NOT_2_out, C20_out);
  or OR_1 (OR_1_out, AND_3_out, AND_2_out, AND_1_out);
  Clock clock_1 (.out(clock_1_out));
  or _0R_2 (_0R_2_out, AND_4_out, AND_5_out);
  and AND_8 (AND_8_out, C10_out, C20_out);
  and AND_9 (AND_9_out, NOT_1_out, OR_4_out, NOT_2_out);
  D_Flip_Flop Q_0 (.clk(clock_1_out), .D(OR_1_out), .Q(Q_0_q), .Qn(Q_0_qn), .reset(undriven));  // open: preset, en
  D_Flip_Flop Q_1 (.clk(clock_1_out), .D(_0R_2_out), .Q(Q_1_q), .Qn(Q_1_qn));  // open: preset, en, reset
  or OR_5 (OR_5_out, AND_8_out, AND_9_out);
  and AND_1 (AND_1_out, Q_0_qn, C20_out, NOT_1_out);
  and AND_2 (AND_2_out, NOT_2_out, C10_out, Q_0_qn);
  or OR_4 (OR_4_out, Q_1_q, Q_0_q);
  and AND_4 (AND_4_out, C10_out, Q_1_qn);
  and AND_3 (AND_3_out, C20_out, Q_0_q, NOT_1_out, Q_1_qn);
  and AND_7 (AND_7_out, Q_0_q, Q_1_q, C10_out, NOT_2_out);
  or OR_6 (OR_6_out, Q_0_q, Q_1_q);
  and AND_5 (AND_5_out, C20_out, NOT_1_out, Q_0_qn, Q_1_q);
  and AND_6 (AND_6_out, NOT_1_out, C20_out, Q_0_q);
  and AND_10 (AND_10_out, Q_0_qn, Q_1_qn);
  or _0R_3 (_0R_3_out, AND_6_out, AND_7_out);
  LED led_1 (.in(_0R_3_out));
  LED led_2 (.in(OR_6_out));
  LED led_3 (.in(OR_5_out));
  LED led_4 (.in(AND_10_out));

  // Notes on the sheet:
  //   NEXT COIN
  //   DISPENSE
  //   RETURN
  //   READY
endmodule
